// Logisim project alu.circ as structural Verilog: 3 circuits, main circuit alu
module alu (
  input  [31:0] A,
  input  [31:0] B,
  input  [3:0] ALUSel,
  output [31:0] Result
);

  wire less;
  wire [4:0] bit_extender_1_out, bit_extender_2_out, bit_extender_3_out;
  wire [31:0] add0, bit_extender_4_out, bitAnd0, bitOr0, mul, mulh, mulhu, mult0, mulu, shr, signShl, sub0,
       unsignShl;
  wire [63:0] bit_extender_5_out, bit_extender_6_out, bit_extender_7_out, bit_extender_8_out;

  Adder #(.width(32)) adder_1 (.a(A), .b(B), .out(add0));  // open: cin, cout
  Bit_Extender #(.in_width(32), .out_width(5)) bit_extender_1 (.in(B), .out(bit_extender_1_out));
  Bit_Extender #(.in_width(32), .out_width(5)) bit_extender_2 (.in(B), .out(bit_extender_2_out));
  Bit_Extender #(.in_width(32), .out_width(5)) bit_extender_3 (.in(B), .out(bit_extender_3_out));
  Shifter #(.shift("lr"), .width(32)) shifter_1 (.in(A), .\dist (bit_extender_1_out), .out(signShl));
  Shifter #(.shift("ar"), .width(32)) shifter_2 (.in(A), .\dist (bit_extender_2_out), .out(unsignShl));
  Shifter #(.width(32)) shifter_3 (.in(A), .\dist (bit_extender_3_out), .out(shr));
  assign bit_extender_4_out = {{31{1'b0}}, less};  // Bit_Extender bit_extender_4
  BitAdder4 bitadder4_1 (
    .InputA0(A[0]), .InputA1(A[1]), .InputA2(A[2]), .InputA3(A[3]), .InputB0(B[0]), .InputB1(B[1]),
    .InputB2(B[2]), .InputB3(B[3]), .Outp0(bitAnd0[0]), .Outp1(bitAnd0[1]), .Outp2(bitAnd0[2]),
    .Outp3(bitAnd0[3]));
  BitAdder4 bitadder4_2 (
    .InputA0(A[4]), .InputA1(A[5]), .InputA2(A[6]), .InputA3(A[7]), .InputB0(B[4]), .InputB1(B[5]),
    .InputB2(B[6]), .InputB3(B[7]), .Outp0(bitAnd0[4]), .Outp1(bitAnd0[5]), .Outp2(bitAnd0[6]),
    .Outp3(bitAnd0[7]));
  BitAdder4 bitadder4_3 (
    .InputA0(A[8]), .InputA1(A[9]), .InputA2(A[10]), .InputA3(A[11]), .InputB0(B[8]), .InputB1(B[9]),
    .InputB2(B[10]), .InputB3(B[11]), .Outp0(bitAnd0[8]), .Outp1(bitAnd0[9]), .Outp2(bitAnd0[10]),
    .Outp3(bitAnd0[11]));
  BitAdder4 bitadder4_4 (
    .InputA0(A[12]), .InputA1(A[13]), .InputA2(A[14]), .InputA3(A[15]), .InputB0(B[12]), .InputB1(B[13]),
    .InputB2(B[14]), .InputB3(B[15]), .Outp0(bitAnd0[12]), .Outp1(bitAnd0[13]), .Outp2(bitAnd0[14]),
    .Outp3(bitAnd0[15]));
  BitAdder4 bitadder4_5 (
    .InputA0(A[16]), .InputA1(A[17]), .InputA2(A[18]), .InputA3(A[19]), .InputB0(B[16]), .InputB1(B[17]),
    .InputB2(B[18]), .InputB3(B[19]), .Outp0(bitAnd0[16]), .Outp1(bitAnd0[17]), .Outp2(bitAnd0[18]),
    .Outp3(bitAnd0[19]));
  BitAdder4 bitadder4_6 (
    .InputA0(A[20]), .InputA1(A[21]), .InputA2(A[22]), .InputA3(A[23]), .InputB0(B[20]), .InputB1(B[21]),
    .InputB2(B[22]), .InputB3(B[23]), .Outp0(bitAnd0[20]), .Outp1(bitAnd0[21]), .Outp2(bitAnd0[22]),
    .Outp3(bitAnd0[23]));
  BitAdder4 bitadder4_7 (
    .InputA0(A[24]), .InputA1(A[25]), .InputA2(A[26]), .InputA3(A[27]), .InputB0(B[24]), .InputB1(B[25]),
    .InputB2(B[26]), .InputB3(B[27]), .Outp0(bitAnd0[24]), .Outp1(bitAnd0[25]), .Outp2(bitAnd0[26]),
    .Outp3(bitAnd0[27]));
  BitAdder4 bitadder4_8 (
    .InputA0(A[28]), .InputA1(A[29]), .InputA2(A[30]), .InputA3(A[31]), .InputB0(B[28]), .InputB1(B[29]),
    .InputB2(B[30]), .InputB3(B[31]), .Outp0(bitAnd0[28]), .Outp1(bitAnd0[29]), .Outp2(bitAnd0[30]),
    .Outp3(bitAnd0[31]));
  assign bit_extender_5_out = {{32{A[31]}}, A};  // Bit_Extender bit_extender_5
  assign bit_extender_6_out = {{32{B[31]}}, B};  // Bit_Extender bit_extender_6
  assign bit_extender_7_out = {{32{1'b0}}, A};  // Bit_Extender bit_extender_7
  assign bit_extender_8_out = {{32{1'b0}}, B};  // Bit_Extender bit_extender_8
  Multiplexer #(.enable("false"), .select(4), .width(32)) multiplexer_1 (
    .in0(add0), .in1(bitAnd0), .in2(A), .in3(bitOr0), .in4(signShl), .in5(unsignShl), .in6(shr),
    .in7(bit_extender_4_out), .in10(mul), .in11(mulhu), .in12(sub0), .in13(B), .in14(mulh), .out(Result),
    .sel(ALUSel));  // open: in8, in9, in15
  Comparator #(.width(32)) comparator_1 (.a(A), .b(B), .lt(less));  // open: gt, eq
  Multiplier #(.width(64)) multiplier_1 (
    .a(bit_extender_5_out), .b(bit_extender_6_out), .out({mulh, mul}));  // open: cin, cout
  Multiplier #(.width(64)) multiplier_2 (
    .a(bit_extender_7_out), .b(bit_extender_8_out), .out({mulhu, mulu}));  // open: cin, cout
  Multiplier #(.width(32)) multiplier_3 (.a(A), .b(B), .out(mult0));  // open: cin, cout
  Subtractor #(.width(32)) subtractor_1 (.a(A), .b(B), .out(sub0));  // open: bin, bout
  bitOr4 bitor4_1 (
    .InputA0(A[0]), .InputA1(A[1]), .InputA2(A[2]), .InputA3(A[3]), .InputB0(B[0]), .InputB1(B[1]),
    .InputB2(B[2]), .InputB3(B[3]), .Outp0(bitOr0[0]), .Outp1(bitOr0[1]), .Outp2(bitOr0[2]), .Outp3(bitOr0[3]));
  bitOr4 bitor4_2 (
    .InputA0(A[4]), .InputA1(A[5]), .InputA2(A[6]), .InputA3(A[7]), .InputB0(B[4]), .InputB1(B[5]),
    .InputB2(B[6]), .InputB3(B[7]), .Outp0(bitOr0[4]), .Outp1(bitOr0[5]), .Outp2(bitOr0[6]), .Outp3(bitOr0[7]));
  bitOr4 bitor4_3 (
    .InputA0(A[8]), .InputA1(A[9]), .InputA2(A[10]), .InputA3(A[11]), .InputB0(B[8]), .InputB1(B[9]),
    .InputB2(B[10]), .InputB3(B[11]), .Outp0(bitOr0[8]), .Outp1(bitOr0[9]), .Outp2(bitOr0[10]),
    .Outp3(bitOr0[11]));
  bitOr4 bitor4_4 (
    .InputA0(A[12]), .InputA1(A[13]), .InputA2(A[14]), .InputA3(A[15]), .InputB0(B[12]), .InputB1(B[13]),
    .InputB2(B[14]), .InputB3(B[15]), .Outp0(bitOr0[12]), .Outp1(bitOr0[13]), .Outp2(bitOr0[14]),
    .Outp3(bitOr0[15]));
  bitOr4 bitor4_5 (
    .InputA0(A[16]), .InputA1(A[17]), .InputA2(A[18]), .InputA3(A[19]), .InputB0(B[16]), .InputB1(B[17]),
    .InputB2(B[18]), .InputB3(B[19]), .Outp0(bitOr0[16]), .Outp1(bitOr0[17]), .Outp2(bitOr0[18]),
    .Outp3(bitOr0[19]));
  bitOr4 bitor4_6 (
    .InputA0(A[20]), .InputA1(A[21]), .InputA2(A[22]), .InputA3(A[23]), .InputB0(B[20]), .InputB1(B[21]),
    .InputB2(B[22]), .InputB3(B[23]), .Outp0(bitOr0[20]), .Outp1(bitOr0[21]), .Outp2(bitOr0[22]),
    .Outp3(bitOr0[23]));
  bitOr4 bitor4_7 (
    .InputA0(A[24]), .InputA1(A[25]), .InputA2(A[26]), .InputA3(A[27]), .InputB0(B[24]), .InputB1(B[25]),
    .InputB2(B[26]), .InputB3(B[27]), .Outp0(bitOr0[24]), .Outp1(bitOr0[25]), .Outp2(bitOr0[26]),
    .Outp3(bitOr0[27]));
  bitOr4 bitor4_8 (
    .InputA0(A[28]), .InputA1(A[29]), .InputA2(A[30]), .InputA3(A[31]), .InputB0(B[28]), .InputB1(B[29]),
    .InputB2(B[30]), .InputB3(B[31]), .Outp0(bitOr0[28]), .Outp1(bitOr0[29]), .Outp2(bitOr0[30]),
    .Outp3(bitOr0[31]));

  // Other names for the same wires on the sheet: resA[31:0] = A; resB[31:0] = B

  // Notes on the sheet:
  //   INPUTS to your circuit
  //   DON'T CHANGE THE LOCATIONS OF THE INPUTS AND OUTPUTS!
  //   OUTPUT from your circuit
endmodule

module BitAdder4 (
  input  InputA0,
  input  InputA1,
  input  InputA2,
  input  InputA3,
  input  InputB0,
  input  InputB1,
  input  InputB2,
  input  InputB3,
  output Outp0,
  output Outp1,
  output Outp2,
  output Outp3
);

  and and_1 (Outp1, InputA1, InputB1);
  and and_2 (Outp2, InputA2, InputB2);
  and and_3 (Outp3, InputA3, InputB3);
  and and_4 (Outp0, InputA0, InputB0);
endmodule

module bitOr4 (
  input  InputA0,
  input  InputA1,
  input  InputA2,
  input  InputA3,
  input  InputB0,
  input  InputB1,
  input  InputB2,
  input  InputB3,
  output Outp0,
  output Outp1,
  output Outp2,
  output Outp3
);

  xor xor_1 (Outp1, InputA1, InputB1);
  xor xor_2 (Outp0, InputA0, InputB0);
  xor xor_3 (Outp2, InputA2, InputB2);
  xor xor_4 (Outp3, InputA3, InputB3);
endmodule
