// Logisim project control_logic.circ as structural Verilog: 1 circuit, main circuit control_logic
module control_logic (
  input  [31:0] inst,
  input  BrEq,
  input  BrLt,
  output PCSel,
  output RegWEn,
  output [2:0] ImmSel,
  output BrUn,
  output ASel,
  output BSel,
  output [3:0] ALUSel,
  output MemRW,
  output [1:0] WBSel,
  output CSRSel,
  output CSRWen,
  output lb,
  output lh,
  output sb,
  output sh
);

  wire AIUPCopcode, ALUIopcode, and_1_out, and_2_out, and_3_out, and_4_out, and_5_out, and_6_out,
       comparator_11_eq, comparator_12_eq, func3_0, func3_1, func3_2, func3_3, func3_4, func3_5, func3_6,
       func3_7, ImmSel_SB, ImmSel_U, ImmSel_UJ, isMul, isMulh, isSra, isSub, Jalropcode, JUIopcode, LIopcode,
       not_1_out, not_2_out, not_3_out, or_1_out, or_3_out, or_7_out, or_11_out, Ropcode, WBSel_ALUout,
       WBSel_PC4;
  wire [1:0] multiplexer_6_out, multiplexer_8_out;
  wire [2:0] multiplexer_1_out, multiplexer_2_out, multiplexer_3_out, multiplexer_4_out;
  wire [3:0] multiplexer_7_out, multiplexer_9_out, multiplexer_10_out, multiplexer_12_out, multiplexer_13_out;

  and and_1 (and_1_out, ImmSel_SB, BrEq, func3_0);
  not not_1 (not_1_out, BrEq);
  not not_2 (not_2_out, BrLt);
  not not_3 (not_3_out, BrLt);
  and and_2 (and_2_out, func3_1, ImmSel_SB, not_1_out);
  and and_3 (and_3_out, ImmSel_SB, func3_4, BrLt);
  and and_4 (and_4_out, ImmSel_SB, func3_6, BrLt);
  and and_5 (and_5_out, ImmSel_SB, func3_5, not_2_out);
  and and_6 (and_6_out, ImmSel_SB, func3_7, not_3_out);
  or or_1 (or_1_out, Jalropcode, ImmSel_UJ);
  or or_2 (ASel, ImmSel_SB, JUIopcode, ImmSel_UJ);
  or or_3 (or_3_out, and_1_out, and_2_out, and_3_out, and_4_out, and_5_out, and_6_out);
  or or_4 (BSel, ALUIopcode, LIopcode, ImmSel_SB, Jalropcode, JUIopcode, AIUPCopcode, ImmSel_UJ);
  Comparator #(.width(7)) comparator_1 (.a(inst[6:0]), .b(7'b1100011), .eq(ImmSel_SB));  // open: gt, lt
  Comparator #(.width(7)) comparator_2 (.a(inst[6:0]), .b(7'b1100111), .eq(Jalropcode));  // open: gt, lt
  Comparator #(.width(7)) comparator_3 (.a(inst[6:0]), .b(7'b1110011), .eq(CSRWen));  // open: gt, lt
  Comparator #(.width(7)) comparator_4 (.a(inst[6:0]), .b(7'b1101111), .eq(ImmSel_UJ));  // open: gt, lt
  or or_5 (PCSel, or_3_out, or_1_out);
  Comparator #(.width(7)) comparator_5 (.a(inst[6:0]), .b(7'b0110111), .eq(AIUPCopcode));  // open: gt, lt
  Comparator #(.width(7)) comparator_6 (.a(inst[6:0]), .b(7'b0010111), .eq(JUIopcode));  // open: gt, lt
  Comparator #(.width(7)) comparator_7 (.a(inst[6:0]), .b(7'b0100011), .eq(MemRW));  // open: gt, lt
  Comparator #(.width(7)) comparator_8 (.a(inst[6:0]), .b(7'b0010011), .eq(ALUIopcode));  // open: gt, lt
  Multiplexer #(.enable("false"), .width(3)) multiplexer_1 (
    .in0(3'b000), .in1(3'b001), .out(multiplexer_1_out), .sel(MemRW));
  or or_6 (ImmSel_U, AIUPCopcode, JUIopcode);
  or or_7 (or_7_out, func3_6, func3_7);
  Multiplexer #(.enable("false"), .width(3)) multiplexer_2 (
    .in0(multiplexer_1_out), .in1(3'b010), .out(multiplexer_2_out), .sel(ImmSel_SB));
  and and_7 (CSRSel, CSRWen, func3_5);
  Multiplexer #(.enable("false"), .width(3)) multiplexer_3 (
    .in0(multiplexer_2_out), .in1(3'b011), .out(multiplexer_3_out), .sel(ImmSel_U));
  and and_8 (BrUn, ImmSel_SB, or_7_out);
  Multiplexer #(.enable("false"), .width(3)) multiplexer_4 (
    .in0(multiplexer_3_out), .in1(3'b100), .out(multiplexer_4_out), .sel(ImmSel_UJ));
  Multiplexer #(.enable("false"), .width(3)) multiplexer_5 (
    .in0(multiplexer_4_out), .in1(3'b101), .out(ImmSel), .sel(CSRSel));
  Comparator #(.width(7)) comparator_9 (.a(inst[6:0]), .b(7'b0000011), .eq(LIopcode));  // open: gt, lt
  Comparator #(.width(7)) comparator_10 (.a(inst[6:0]), .b(7'b0110011), .eq(Ropcode));  // open: gt, lt
  or or_8 (RegWEn, ImmSel_UJ, AIUPCopcode, JUIopcode, Jalropcode, Ropcode, LIopcode, ALUIopcode);
  Multiplexer #(.enable("false"), .width(2)) multiplexer_6 (
    .in0(2'b00), .in1(2'b01), .out(multiplexer_6_out), .sel(WBSel_ALUout));
  Comparator #(.width(7)) comparator_11 (.a(inst[31:25]), .b(7'b0000001), .eq(comparator_11_eq));  // open: gt, lt
  Comparator #(.width(7)) comparator_12 (.a(inst[31:25]), .b(7'b0100000), .eq(comparator_12_eq));  // open: gt, lt
  Multiplexer #(.enable("false"), .select(3), .width(4)) multiplexer_7 (
    .in0(4'b0000), .in1(4'b0110), .in2(4'b0111), .in3(4'b1011), .in4(4'b0011), .in5(4'b0100), .in6(4'b0010),
    .in7(4'b0001), .out(multiplexer_7_out), .sel(inst[14:12]));
  or or_9 (WBSel_ALUout, JUIopcode, Ropcode, ALUIopcode);
  or or_10 (WBSel_PC4, Jalropcode, ImmSel_UJ);
  Multiplexer #(.enable("false"), .width(2)) multiplexer_8 (
    .in0(multiplexer_6_out), .in1(2'b10), .out(multiplexer_8_out), .sel(WBSel_PC4));
  Comparator #(.width(3)) comparator_13 (.a(inst[14:12]), .b(3'b001), .eq(func3_1));  // open: gt, lt
  Comparator #(.width(3)) comparator_14 (.a(inst[14:12]), .b(3'b010), .eq(func3_2));  // open: gt, lt
  Comparator #(.width(3)) comparator_15 (.a(inst[14:12]), .b(3'b011), .eq(func3_3));  // open: gt, lt
  Comparator #(.width(3)) comparator_16 (.a(inst[14:12]), .b(3'b100), .eq(func3_4));  // open: gt, lt
  Multiplexer #(.enable("false"), .width(4)) multiplexer_9 (
    .in0(multiplexer_7_out), .in1(4'b1010), .out(multiplexer_9_out), .sel(isMul));
  Multiplexer #(.enable("false"), .width(4)) multiplexer_10 (
    .in0(multiplexer_9_out), .in1(4'b1100), .out(multiplexer_10_out), .sel(isSub));
  Multiplexer #(.enable("false"), .width(2)) multiplexer_11 (
    .in0(multiplexer_8_out), .in1(2'b11), .out(WBSel), .sel(AIUPCopcode));
  and and_9 (isMul, comparator_11_eq, Ropcode, func3_0);
  and and_10 (isMulh, comparator_11_eq, Ropcode, func3_1);
  and and_11 (isSra, comparator_12_eq, Ropcode, func3_5);
  and and_12 (isSub, comparator_12_eq, Ropcode, func3_0);
  Multiplexer #(.enable("false"), .width(4)) multiplexer_12 (
    .in0(multiplexer_10_out), .in1(4'b1110), .out(multiplexer_12_out), .sel(isMulh));
  Multiplexer #(.enable("false"), .width(4)) multiplexer_13 (
    .in0(multiplexer_12_out), .in1(4'b0101), .out(multiplexer_13_out), .sel(isSra));
  Comparator #(.width(3)) comparator_17 (.a(inst[14:12]), .b(3'b000), .eq(func3_0));  // open: gt, lt
  Comparator #(.width(3)) comparator_18 (.a(inst[14:12]), .b(3'b101), .eq(func3_5));  // open: gt, lt
  Comparator #(.width(3)) comparator_19 (.a(inst[14:12]), .b(3'b110), .eq(func3_6));  // open: gt, lt
  Comparator #(.width(3)) comparator_20 (.a(inst[14:12]), .b(3'b111), .eq(func3_7));  // open: gt, lt
  Multiplexer #(.enable("false"), .width(4)) multiplexer_14 (
    .in0(4'b0000), .in1(multiplexer_13_out), .out(ALUSel), .sel(or_11_out));
  or or_11 (or_11_out, Ropcode, ALUIopcode);
  and and_13 (lb, LIopcode, func3_0);
  and and_14 (lh, LIopcode, func3_1);
  and and_15 (sb, MemRW, func3_0);
  and and_16 (sh, MemRW, func3_1);

  // Other names for the same wires on the sheet: CSRopcode = CSRWen; ImmSel_CSRRWI = CSRSel; opcode[6:0] = inst[6:0];
  //   rd[4:0] = inst[11:7]; func3[2:0] = inst[14:12]; rs1[4:0] = inst[19:15]; rs2[4:0] = inst[24:20];
  //   func7[6:0] = inst[31:25]; SBopcode = ImmSel_SB; ImmSel_S = MemRW; Sopcode = MemRW; UJopcode = ImmSel_UJ;
  //   WBSel_Imm = AIUPCopcode

  // Notes on the sheet:
  //   1. PCSel
  //   4. ASel
  //   5. BSel
  //   INPUTS to your circuit
  //   Instruction Decoder
  //   beq
  //   bnq
  //   blt
  //   bltu
  //   bge
  //   bgeu
  //   Opcode Decoder
  //   DON'T CHANGE THE LOCATIONS OF THE INPUTS AND OUTPUTS!
  //   OUTPUT from your circuit
  //   3. ImmSel
  //   2. RegWen and CSRWen
  //   6. ALUSel
  //   7. WBSel
  //   Func3 decoder
  //   8. L and S
endmodule
