// Logisim project regfile.circ as structural Verilog: 1 circuit, main circuit regfile
module regfile (
  input  [4:0] rs1,
  input  [4:0] rs2,
  input  [4:0] rd,
  input  [31:0] Write_Data,
  input  RegWEn,
  input  clk,
  output [31:0] ra,
  output [31:0] sp,
  output [31:0] t0,
  output [31:0] t1,
  output [31:0] t2,
  output [31:0] s0,
  output [31:0] s1,
  output [31:0] a0,
  output [31:0] Read_Data_1,
  output [31:0] Read_Data_2
);

  wire demultiplexer_1_out1, demultiplexer_1_out2, demultiplexer_1_out3, demultiplexer_1_out4,
       demultiplexer_1_out5, demultiplexer_1_out6, demultiplexer_1_out7, demultiplexer_1_out8,
       demultiplexer_1_out9, demultiplexer_1_out10, demultiplexer_1_out11, demultiplexer_1_out12,
       demultiplexer_1_out13, demultiplexer_1_out14, demultiplexer_1_out15, demultiplexer_1_out16,
       demultiplexer_1_out17, demultiplexer_1_out18, demultiplexer_1_out19, demultiplexer_1_out20,
       demultiplexer_1_out21, demultiplexer_1_out22, demultiplexer_1_out23, demultiplexer_1_out24,
       demultiplexer_1_out25, demultiplexer_1_out26, demultiplexer_1_out27, demultiplexer_1_out28,
       demultiplexer_1_out29, demultiplexer_1_out30, demultiplexer_1_out31;
  wire [31:0] register_1_q, register_4_q, register_5_q, register_12_q, register_13_q, register_14_q,
       register_15_q, register_16_q, register_17_q, register_18_q, register_19_q, register_20_q,
       register_21_q, register_22_q, register_23_q, register_24_q, register_25_q, register_26_q,
       register_27_q, register_28_q, register_29_q, register_30_q, register_31_q, register_32_q;

  Demultiplexer #(.enable("false"), .select(5)) demultiplexer_1 (
    .out1(demultiplexer_1_out1), .out2(demultiplexer_1_out2), .out3(demultiplexer_1_out3),
    .out4(demultiplexer_1_out4), .out5(demultiplexer_1_out5), .out6(demultiplexer_1_out6),
    .out7(demultiplexer_1_out7), .out8(demultiplexer_1_out8), .out9(demultiplexer_1_out9),
    .out10(demultiplexer_1_out10), .out11(demultiplexer_1_out11), .out12(demultiplexer_1_out12),
    .out13(demultiplexer_1_out13), .out14(demultiplexer_1_out14), .out15(demultiplexer_1_out15),
    .out16(demultiplexer_1_out16), .out17(demultiplexer_1_out17), .out18(demultiplexer_1_out18),
    .out19(demultiplexer_1_out19), .out20(demultiplexer_1_out20), .out21(demultiplexer_1_out21),
    .out22(demultiplexer_1_out22), .out23(demultiplexer_1_out23), .out24(demultiplexer_1_out24),
    .out25(demultiplexer_1_out25), .out26(demultiplexer_1_out26), .out27(demultiplexer_1_out27),
    .out28(demultiplexer_1_out28), .out29(demultiplexer_1_out29), .out30(demultiplexer_1_out30),
    .out31(demultiplexer_1_out31), .in(RegWEn), .sel(rd));  // open: out0
  Register #(.width(32)) register_1 (.D({32{1'b0}}), .clk(clk), .Q(register_1_q));  // open: en, clr
  Register #(.width(32)) register_2 (.D(Write_Data), .en(demultiplexer_1_out1), .clk(clk), .Q(ra));  // open: clr
  Register #(.width(32)) register_3 (.D(Write_Data), .en(demultiplexer_1_out2), .clk(clk), .Q(sp));  // open: clr
  Register #(.width(32)) register_4 (
    .D(Write_Data), .en(demultiplexer_1_out3), .clk(clk), .Q(register_4_q));  // open: clr
  Register #(.width(32)) register_5 (
    .D(Write_Data), .en(demultiplexer_1_out4), .clk(clk), .Q(register_5_q));  // open: clr
  Register #(.width(32)) register_6 (.D(Write_Data), .en(demultiplexer_1_out5), .clk(clk), .Q(t0));  // open: clr
  Register #(.width(32)) register_7 (.D(Write_Data), .en(demultiplexer_1_out6), .clk(clk), .Q(t1));  // open: clr
  Register #(.width(32)) register_8 (.D(Write_Data), .en(demultiplexer_1_out7), .clk(clk), .Q(t2));  // open: clr
  Register #(.width(32)) register_9 (.D(Write_Data), .en(demultiplexer_1_out8), .clk(clk), .Q(s0));  // open: clr
  Register #(.width(32)) register_10 (.D(Write_Data), .en(demultiplexer_1_out9), .clk(clk), .Q(s1));  // open: clr
  Register #(.width(32)) register_11 (.D(Write_Data), .en(demultiplexer_1_out10), .clk(clk), .Q(a0));  // open: clr
  Register #(.width(32)) register_12 (
    .D(Write_Data), .en(demultiplexer_1_out11), .clk(clk), .Q(register_12_q));  // open: clr
  Register #(.width(32)) register_13 (
    .D(Write_Data), .en(demultiplexer_1_out12), .clk(clk), .Q(register_13_q));  // open: clr
  Register #(.width(32)) register_14 (
    .D(Write_Data), .en(demultiplexer_1_out13), .clk(clk), .Q(register_14_q));  // open: clr
  Register #(.width(32)) register_15 (
    .D(Write_Data), .en(demultiplexer_1_out14), .clk(clk), .Q(register_15_q));  // open: clr
  Register #(.width(32)) register_16 (
    .D(Write_Data), .en(demultiplexer_1_out15), .clk(clk), .Q(register_16_q));  // open: clr
  Register #(.width(32)) register_17 (
    .D(Write_Data), .en(demultiplexer_1_out16), .clk(clk), .Q(register_17_q));  // open: clr
  Register #(.width(32)) register_18 (
    .D(Write_Data), .en(demultiplexer_1_out17), .clk(clk), .Q(register_18_q));  // open: clr
  Register #(.width(32)) register_19 (
    .D(Write_Data), .en(demultiplexer_1_out18), .clk(clk), .Q(register_19_q));  // open: clr
  Register #(.width(32)) register_20 (
    .D(Write_Data), .en(demultiplexer_1_out19), .clk(clk), .Q(register_20_q));  // open: clr
  Register #(.width(32)) register_21 (
    .D(Write_Data), .en(demultiplexer_1_out20), .clk(clk), .Q(register_21_q));  // open: clr
  Register #(.width(32)) register_22 (
    .D(Write_Data), .en(demultiplexer_1_out21), .clk(clk), .Q(register_22_q));  // open: clr
  Register #(.width(32)) register_23 (
    .D(Write_Data), .en(demultiplexer_1_out22), .clk(clk), .Q(register_23_q));  // open: clr
  Register #(.width(32)) register_24 (
    .D(Write_Data), .en(demultiplexer_1_out23), .clk(clk), .Q(register_24_q));  // open: clr
  Register #(.width(32)) register_25 (
    .D(Write_Data), .en(demultiplexer_1_out24), .clk(clk), .Q(register_25_q));  // open: clr
  Register #(.width(32)) register_26 (
    .D(Write_Data), .en(demultiplexer_1_out25), .clk(clk), .Q(register_26_q));  // open: clr
  Register #(.width(32)) register_27 (
    .D(Write_Data), .en(demultiplexer_1_out26), .clk(clk), .Q(register_27_q));  // open: clr
  Register #(.width(32)) register_28 (
    .D(Write_Data), .en(demultiplexer_1_out27), .clk(clk), .Q(register_28_q));  // open: clr
  Register #(.width(32)) register_29 (
    .D(Write_Data), .en(demultiplexer_1_out28), .clk(clk), .Q(register_29_q));  // open: clr
  Register #(.width(32)) register_30 (
    .D(Write_Data), .en(demultiplexer_1_out29), .clk(clk), .Q(register_30_q));  // open: clr
  Register #(.width(32)) register_31 (
    .D(Write_Data), .en(demultiplexer_1_out30), .clk(clk), .Q(register_31_q));  // open: clr
  Register #(.width(32)) register_32 (
    .D(Write_Data), .en(demultiplexer_1_out31), .clk(clk), .Q(register_32_q));  // open: clr
  Multiplexer #(.enable("false"), .select(5), .width(32)) multiplexer_1 (
    .in0(register_1_q), .in1(ra), .in2(sp), .in3(register_4_q), .in4(register_5_q), .in5(t0), .in6(t1),
    .in7(t2), .in8(s0), .in9(s1), .in10(a0), .in11(register_12_q), .in12(register_13_q),
    .in13(register_14_q), .in14(register_15_q), .in15(register_16_q), .in16(register_17_q),
    .in17(register_18_q), .in18(register_19_q), .in19(register_20_q), .in20(register_21_q),
    .in21(register_22_q), .in22(register_23_q), .in23(register_24_q), .in24(register_25_q),
    .in25(register_26_q), .in26(register_27_q), .in27(register_28_q), .in28(register_29_q),
    .in29(register_30_q), .in30(register_31_q), .in31(register_32_q), .out(Read_Data_1), .sel(rs1));
  Multiplexer #(.enable("false"), .select(5), .width(32)) multiplexer_2 (
    .in0(register_1_q), .in1(ra), .in2(sp), .in3(register_4_q), .in4(register_5_q), .in5(t0), .in6(t1),
    .in7(t2), .in8(s0), .in9(s1), .in10(a0), .in11(register_12_q), .in12(register_13_q),
    .in13(register_14_q), .in14(register_15_q), .in15(register_16_q), .in16(register_17_q),
    .in17(register_18_q), .in18(register_19_q), .in19(register_20_q), .in20(register_21_q),
    .in21(register_22_q), .in22(register_23_q), .in23(register_24_q), .in24(register_25_q),
    .in25(register_26_q), .in26(register_27_q), .in27(register_28_q), .in28(register_29_q),
    .in29(register_30_q), .in30(register_31_q), .in31(register_32_q), .out(Read_Data_2), .sel(rs2));

  // Other names for the same wires on the sheet: read_data1[31:0] = Read_Data_1; read_data2[31:0] = Read_Data_2;
  //   read_reg1[4:0] = rs1; read_reg2[4:0] = rs2; write_en = RegWEn; write_reg[4:0] = rd

  // Notes on the sheet:
  //   INPUTS to your circuit
  //   DON'T CHANGE THE LOCATIONS OF THE INPUTS AND OUTPUTS!
  //   These are DEBUG/TEST outputs from your circuit.
  //   OUTPUTS from your circuit
endmodule
